# Fritzing sketch DisplaySchematic (saved by Fritzing 0.9.2b)

parts:
  Arduino_Mega = Arduino Mega ADK (Rev3)
  ILI9340 = 2.2" TFT with MicroSD Breakout

nets:
  N1: Arduino_Mega.D4_PWM, ILI9340.CS
  5V: Arduino_Mega.5V, ILI9340.BL, ILI9340.VIN
  N2: Arduino_Mega.D30, ILI9340.RST
  N3: Arduino_Mega.D32, ILI9340.SDCS
  N4: Arduino_Mega.D50/MISO, ILI9340.MISO
  N5: Arduino_Mega.D51/MOSI, ILI9340.MOSI
  N6: Arduino_Mega.D52/SCK, ILI9340.SCK
  GND: Arduino_Mega.GND, ILI9340.GND

custom parts:
  2.2" TFT with MicroSD Breakout: 2.2" TFT Display with HX8340B Controller and MicroSD Card
