# Fritzing sketch Konditionering (saved by Fritzing 0.9.2b)
breadboards: 1

parts:
  U1 = OP482 - Low Power, High Speed JFET Quad Operational Amplifier [part_number=OP482]
  S1 = Pushbutton [package="[THT]"]
  S2 = Pushbutton [package="[THT]"]
  C1 = Ceramic Capacitor [capacitance=100nF package="200 mil [THT, multilayer]"]
  C2 = Ceramic Capacitor [capacitance=100nF package="200 mil [THT, multilayer]"]
  R1 = Resistor [tolerance=±5% resistance=10k package="2512 [SMD]"]
  R2 = Resistor [tolerance=±5% resistance=10k package="2512 [SMD]"]
  C4 = Ceramic Capacitor [capacitance=100nF package="200 mil [THT, multilayer]"]
  R3 = Resistor [tolerance=±5% resistance=100k package="2512 [SMD]"]
  C7 = Ceramic Capacitor [package="0603 [SMD, multilayer]"]
  C8 = Ceramic Capacitor [package="0603 [SMD, multilayer]"]
  C9 = Ceramic Capacitor [package="100 mil [THT, multilayer]"]
  R8 = Resistor [tolerance=±5% resistance=100k package="2512 [SMD]"]
  R9 = Resistor [tolerance=±5% resistance=1M package="2512 [SMD]"]
  R10 = Resistor [tolerance=±5% resistance=1k package="2512 [SMD]"]
  R11 = Resistor [tolerance=±5% resistance=100k package="2512 [SMD]"]
  R12 = Resistor [tolerance=±5% resistance=100k package="2512 [SMD]"]
  R13 = Resistor [tolerance=±5% resistance=100k package="2512 [SMD]"]
  R14 = Resistor [tolerance=±5% resistance=1M package="2512 [SMD]"]
  Signal_In = Header 1 [part_number="Signal In" package=smtso-256-et]
  IC1 = Hex Inverter Schmitt Trigger SN74HC14 [package="DIP (Dual Inline)"]
  V1 = DC Power [voltage=5V]
  Signal_out(A3) = Header 1 [package=smtso-256-et]
  Signal_out(A4) = Header 1 [package=smtso-256-et]
  Part1 = Arduino Mega 2560 (Rev3)
  TFT1 = 2.2" TFT with MicroSD Breakout
  Part2 = Arduino Motor Shield (Rev3)
  M1 = DC Motor  # not connected

nets:
  N1: U1.OUTA, R13.Pin_1, R14.Pin_0
  N2: U1.-INA, R12.Pin_1, R13.Pin_0
  N3: U1.+INA, R8.Pin_0, Signal_In.1
  N4: U1.V+, R1.Pin_0, R2.Pin_0, IC1.VCC, V1.V+
  N5: U1.+INB, C8.0, R14.Pin_1
  N6: U1.-INB, U1.OUTB, Signal_out(A3).1
  N7: U1.OUTC, R11.Pin_0, Signal_out(A4).1
  N8: U1.-INC, R10.Pin_0, R11.Pin_1
  N9: U1.+INC, C7.0, R9.Pin_0
  N10: U1.V-, S1.Pin_3, S1.Pin_4, S2.Pin_3, S2.Pin_4, C1.0, C2.0, C4.1, C8.1, R9.Pin_1, R10.Pin_1, R12.Pin_0, IC1.3A, IC1.GND, IC1.4A, IC1.5A, IC1.6A, V1.V-
  N11: U1.+IND, C4.0, R3.Pin_1
  N12: U1.-IND, U1.OUTD, C7.1, C9.1
  N13: S1.Pin_1, S1.Pin_2, C1.1, R1.Pin_1, IC1.2A
  N14: S2.Pin_1, S2.Pin_2, C2.1, R2.Pin_1, IC1.1A
  N15: R3.Pin_0, C9.0, R8.Pin_1
  N16: Part1.A0, Part2.A0
  N17: Part1.A1, Part2.A1
  N18: Part1.A2, Part2.A2
  N19: Part1.A3, Part2.A3
  N20: Part1.A4, Part2.A4
  N21: Part1.A5, Part2.A5
  N22: Part1.SCL, Part2.SCL
  N23: Part1.SDA, Part2.SDA
  N24: Part1.AREF, Part2.AREF
  GND: Part1.GND, TFT1.GND, Part2.GND
  N25: Part1.D13_PWM, Part2.D13/DirB
  N26: Part1.D12_PWM, Part2.D12/DirA
  N27: Part1.D11_PWM, Part2.D11_PWM/B
  N28: Part1.D10_PWM, TFT1.CS, Part2.D10_PWM
  N29: Part1.D9_PWM, Part2.D9/BreakeA
  N30: Part1.D8_PWM, TFT1.RST, Part2.D8/BreakeB
  N31: Part1.IOREF, Part2.IOREF#147
  N32: Part1.RESET, Part2.RESET
  3V3: Part1.3V3, Part2.3V3
  5V: Part1.5V, TFT1.BL, TFT1.VIN, Part2.5V
  VIN: Part1.VIN, Part2.VIN
  N33: Part1.D0_RX0, Part2.IOREF#118
  N34: Part1.D1_TX0, Part2.D1/TX
  N35: Part1.D2_PWM, Part2.D2
  N36: Part1.D3_PWM, Part2.D3_PWM/A
  N37: Part1.D4_PWM, TFT1.SDCS, Part2.D4
  N38: Part1.D5_PWM, Part2.D5_PWM
  N39: Part1.D6_PWM, Part2.D6_PWM
  N40: Part1.D7_PWM, Part2.D7
  N41: Part1.D50, TFT1.MOSI
  N42: Part1.D51, TFT1.MISO
  N43: Part1.D52, TFT1.SCK

custom parts:
  Ceramic Capacitor: 0.01 nF multilayered Ceramic Capacitor
  Ceramic Capacitor: 200 nF multilayer Ceramic Capacitor
  2.2" TFT with MicroSD Breakout: 2.2" TFT Display with HX8340B Controller and MicroSD Card
