# Fritzing sketch Prototype (saved by Fritzing 0.9.2b)
breadboards: 1

parts:
  Part1 = Arduino Mega ADK (Rev3)  # not connected
  Part2 = Arduino Motor Shield (Rev3)
  S1 = Pushbutton [package="[THT]"]
  S2 = Pushbutton [package="[THT]"]
  TFT1 = 2.2" TFT with MicroSD Breakout  # not connected
  M1 = DC Motor
  R1 = Resistor [tolerance=±5% resistance=10k package=THT]
  R2 = Resistor [tolerance=±5% resistance=10k package=THT]

nets:
  N1: Part2.GND, R1.Pin_1, R2.Pin_1
  N2: Part2.D2, S1.Pin_3, S1.Pin_4, R1.Pin_0
  N3: Part2.D4, S2.Pin_3, S2.Pin_4, R2.Pin_0
  N4: Part2.A-, M1.pin_2
  N5: Part2.A+, M1.pin_1
  N6: Part2.5V, S1.Pin_1, S1.Pin_2, S2.Pin_1, S2.Pin_2

custom parts:
  2.2" TFT with MicroSD Breakout: 2.2" TFT Display with HX8340B Controller and MicroSD Card
