# Fritzing sketch TimerSchematic (saved by Fritzing 0.9.2b)

parts:
  PCB1 = RTC_DS1302_module
  Part1 = Arduino Mega ADK (Rev3)

nets:
  VCC: PCB1.VCC, Part1.5V
  GND: PCB1.GND, Part1.GND
  N1: PCB1.RST, Part1.D5_PWM
  N2: PCB1.DAT, Part1.D6_PWM
  N3: PCB1.CLK, Part1.D7_PWM

custom parts:
  RTC_DS1302_module: Arduino module DS1302 SPI Real Time Clock
